# Fritzing sketch schematic_4x4 (saved by Fritzing 0.9.3b)
breadboards: 1

parts:
  Arduino = Arduino Uno (Rev3) - ICSP
  4x4_keypad_8_pins_S1_on_module_=_right;_ignore_dots_on_board_shown_here = BUTTONPAD-4X4 [package=buttonpad-4x4]
  LED1 = smd LED [color="Red (633nm)" package="0603 [SMD]"]
  LED2 = smd LED [color="Green (555nm)" package="0603 [SMD]"]

nets:
  N1: Arduino.ICSP_MISO, Arduino.D12/MISO, 4x4_keypad_8_pins_S1_on_module_=_right;_ignore_dots_on_board_shown_here.G$6_SIG2
  N2: Arduino.D10_PWM/SS, 4x4_keypad_8_pins_S1_on_module_=_right;_ignore_dots_on_board_shown_here.G$13_GND
  N3: Arduino.D11_PWM/MOSI, 4x4_keypad_8_pins_S1_on_module_=_right;_ignore_dots_on_board_shown_here.G$13_RED
  N4: Arduino.D2, LED1.anode
  N5: Arduino.D3_PWM, LED2.anode
  N6: Arduino.D4, 4x4_keypad_8_pins_S1_on_module_=_right;_ignore_dots_on_board_shown_here.G$11_GND
  N7: Arduino.D5_PWM, 4x4_keypad_8_pins_S1_on_module_=_right;_ignore_dots_on_board_shown_here.G$11_RED
  N8: Arduino.D6_PWM, 4x4_keypad_8_pins_S1_on_module_=_right;_ignore_dots_on_board_shown_here.G$12_GRN
  N9: Arduino.D7, 4x4_keypad_8_pins_S1_on_module_=_right;_ignore_dots_on_board_shown_here.G$12_GND
  N10: Arduino.GND, LED1.cathode, LED2.cathode
